# Fritzing sketch T0103_LED5_waterLights (saved by Fritzing 0.9.1b)
breadboards: 1

parts:
  J1 = shrouded pin header, 6 pins [form="♂ (shrouded male)"]
  IC1 = IC, DIP package, 8 pins [chip_label=T13]
  R1 = Resistor [tolerance=±5% resistance=1k package=THT]
  LED1 = LED - 5mm [color="Red (633nm)" package="5 mm [THT]"]
  LED2 = LED - 5mm [color="Yellow (585nm)" package="5 mm [THT]"]
  LED3 = LED - 5mm [color="Green (555nm)" package="5 mm [THT]"]
  LED4 = LED - 5mm [color="Blue (430nm)" package="5 mm [THT]"]
  LED5 = LED - 5mm [color="Red (633nm)" package="5 mm [THT]"]
  R2 = Resistor [tolerance=±5% resistance=1k package=THT]
  R3 = Resistor [tolerance=±5% resistance=1k package=THT]
  R4 = Resistor [tolerance=±5% resistance=1k package=THT]
  R5 = Resistor [tolerance=±5% resistance=1k package=THT]

nets:
  N1: J1.pin1, IC1.pin6, LED4.anode
  N2: J1.pin2, IC1.pin7, LED3.anode
  N3: J1.pin3, IC1.pin1
  N4: J1.pin4, IC1.pin4, R1.Pin_1, R2.Pin_1, R3.Pin_1, R4.Pin_1, R5.Pin_1
  N5: J1.pin5, IC1.pin5, LED5.anode
  N6: J1.pin6, IC1.pin8
  N7: IC1.pin2, LED2.anode
  N8: IC1.pin3, LED1.anode
  N9: R1.Pin_0, LED1.cathode
  N10: LED2.cathode, R2.Pin_0
  N11: LED3.cathode, R3.Pin_0
  N12: LED4.cathode, R4.Pin_0
  N13: LED5.cathode, R5.Pin_0
