# Fritzing sketch T0104_Fade_PWM_Breathinglight_V3 (saved by Fritzing 0.9.1b)
breadboards: 1

parts:
  J1 = shrouded pin header, 6 pins [form="♂ (shrouded male)"]
  IC1 = IC, DIP package, 8 pins [chip_label=T13]
  LED1 = LED - 5mm [color="Red (633nm)" package="5 mm [THT]"]
  R1 = Resistor [tolerance=±5% resistance=220 package=THT]
  R2 = Rotary Potentiometer (Small) [maximum_resistance=100kΩ package=THT]

nets:
  N1: J1.pin1, IC1.pin6
  N2: J1.pin2, IC1.pin7
  N3: J1.pin3, IC1.pin1
  N4: J1.pin4, IC1.pin4, R1.Pin_0, R2.leg2
  N5: J1.pin5, IC1.pin5, LED1.anode
  N6: J1.pin6, IC1.pin8, R2.leg1
  N7: IC1.pin2, R2.wiper
  N8: LED1.cathode, R1.Pin_1
