# Fritzing sketch T0202_ServoSweep (saved by Fritzing 0.9.1b)
breadboards: 1

parts:
  J1 = shrouded pin header, 6 pins [form="♂ (shrouded male)"]
  IC1 = IC, DIP package, 8 pins [chip_label=T13]
  J2 = Basic Servo

nets:
  N1: J1.pin1, IC1.pin6
  N2: J1.pin2, IC1.pin7
  N3: J1.pin3, IC1.pin1
  N4: J1.pin4, IC1.pin4, J2.gnd
  N5: J1.pin5, IC1.pin5
  N6: J1.pin6, IC1.pin8, J2.vcc
  N7: IC1.pin3, J2.pulse
