# Fritzing sketch 03_Snow (saved by Fritzing 0.9.1b)
circuit board: 4.93677cm x 4.28483cm
breadboards: 1

parts:
  VCC7 = Pad [width=3 height=8 connect=center]
  GND7 = Pad [width=3 height=8 connect=center]
  C1 = Ceramic Capacitor [capacitance=0.1µF package="0805 [SMD, multilayer]"]
  TINY13 = ATTINY13 [package=so]
  C2 = Ceramic Capacitor [capacitance=0.1µF package="0805 [SMD, multilayer]"]
  R1 = Resistor [tolerance=±5% resistance=220 package="0805 [SMD]"]
  LED1 = smd LED [color="Red (633nm)" package="0805 [SMD]"]
  R2 = Resistor [tolerance=±5% resistance=220 package="0805 [SMD]"]
  LED2 = smd LED [color="Red (633nm)" package="0805 [SMD]"]
  R3 = Resistor [tolerance=±5% resistance=220 package="0805 [SMD]"]
  LED3 = smd LED [color="Red (633nm)" package="0805 [SMD]"]
  R4 = Resistor [tolerance=±5% resistance=220 package="0805 [SMD]"]
  LED4 = smd LED [color="Red (633nm)" package="0805 [SMD]"]
  R5 = Resistor [tolerance=±5% resistance=220 package="0805 [SMD]"]
  LED5 = smd LED [color="Red (633nm)" package="0805 [SMD]"]
  --__-- = double row smd male pin header, 6 pins [form="♂ (male)"]
  J6 = female pin header, 1 pin [form="♀ (female)"]
  J5 = female pin header, 1 pin [form="♀ (female)"]
  J4 = female pin header, 1 pin [form="♀ (female)"]
  J1 = female pin header, 1 pin [form="♀ (female)"]
  J8 = female pin header, 1 pin [form="♀ (female)"]
  J7 = female pin header, 1 pin [form="♀ (female)"]

nets:
  N1: VCC7.pad, C1.0, TINY13.VCC, C2.0, --__--.pin3, J8.pin1
  GND: GND7.pad, C1.1, TINY13.GND, C2.1, LED1.cathode, LED2.cathode, LED3.cathode, LED4.cathode, LED5.cathode, --__--.pin1, J4.pin1
  N2: TINY13.PB5(NRES), --__--.pin6, J1.pin1
  N3: TINY13.PB3(ADC3), R4.Pin_1
  N4: TINY13.PB4(ADC2), R5.Pin_1
  N5: TINY13.PB0(MOSI), R1.Pin_1, --__--.pin2, J5.pin1
  N6: TINY13.PB1(MISO), R2.Pin_1, --__--.pin4, J6.pin1
  N7: TINY13.PB2(SCK_ADC1), R3.Pin_1, --__--.pin5, J7.pin1
  N8: R1.Pin_0, LED1.anode
  N9: R2.Pin_0, LED2.anode
  N10: R3.Pin_0, LED3.anode
  N11: R4.Pin_0, LED4.anode
  N12: R5.Pin_0, LED5.anode

notes:
  ^^
  VCC
  GND
  ||
